# Fritzing sketch Arduino & BT (saved by Fritzing 0.9.2b)
perfboards: 1

parts:
  ARDUINO = Arduino Nano (Rev3.0)
  Data = female pin header, 1 pin [form="♀ (female)"]
  Clock = female pin header, 1 pin [form="♀ (female)"]
  Load = female pin header, 1 pin [form="♀ (female)"]
  Latch = female pin header, 1 pin [form="♀ (female)"]
  OutputEnabled = female pin header, 1 pin [form="♀ (female)"]
  +5v = female pin header, 1 pin [form="♀ (female)"]
  Ground = female pin header, 1 pin [form="♀ (female)"]
  R1 = Resistor [tolerance=±5% resistance=10k package="0805 [SMD]"]
  BT4_0_HM-10 = BT4 hm-10 [chip_label=IC package="SIP (Single Inline) [THT]"]

nets:
  Ground: ARDUINO.GND, Ground.pin1, R1.Pin_0, BT4_0_HM-10.GND
  Load: ARDUINO.A6, Load.pin1
  OC_OE: ARDUINO.A5, OutputEnabled.pin1, R1.Pin_1
  OC_Latch: ARDUINO.A4, Latch.pin1
  Clk: ARDUINO.A3, Clock.pin1
  Data: ARDUINO.A2, Data.pin1
  BT_RX: ARDUINO.A1, BT4_0_HM-10.RXD
  BT_TX: ARDUINO.A0, BT4_0_HM-10.TXD
  VCC 3V: ARDUINO.3V3, BT4_0_HM-10.VCC_+3v
  VCC: +5v.pin1

notes:
  RX - A1
  TX - A0
  GND
  VCC -(3.3v)
