# Fritzing sketch Master (saved by Fritzing 0.9.2b)
breadboards: 1

parts:
  ARDUINO1 = Arduino Nano (Rev3.0)
  Ground1 = female pin header, 1 pin [form="♀ (female)"]
  +5v1 = female pin header, 1 pin [form="♀ (female)"]
  R2 = Resistor [tolerance=±5% resistance=10k package="0805 [SMD]"]
  BT4_0_HM-12 = BT4 hm-10 [chip_label=IC package="SIP (Single Inline) [THT]"]
  Output_Control = 74HC595 [package="DIP16 [THT]"]
  OC_Q9 = TRANSISTOR_NPN [package=to-92]
  OC_R9 = Resistor [tolerance=±5% resistance=10k package="0805 [SMD]"]
  OC_Q10 = TRANSISTOR_NPN [package=to-92]
  OC_R10 = Resistor [tolerance=±5% resistance=10k package="0805 [SMD]"]
  OC_Q11 = TRANSISTOR_NPN [package=to-92]
  OC_R11 = Resistor [tolerance=±5% resistance=10k package="0805 [SMD]"]
  OC_Q12 = TRANSISTOR_NPN [package=to-92]
  OC_R12 = Resistor [tolerance=±5% resistance=10k package="0805 [SMD]"]
  OC_Q13 = TRANSISTOR_NPN [package=to-92]
  OC_R13 = Resistor [tolerance=±5% resistance=10k package="0805 [SMD]"]
  OC_Q14 = TRANSISTOR_NPN [package=to-92]
  OC_R14 = Resistor [tolerance=±5% resistance=10k package="0805 [SMD]"]
  OC_Q15 = TRANSISTOR_NPN [package=to-92]
  OC_R15 = Resistor [tolerance=±5% resistance=10k package="0805 [SMD]"]
  OC_Q16 = TRANSISTOR_NPN [package=to-92]
  OC_R16 = Resistor [tolerance=±5% resistance=10k package="0805 [SMD]"]
  OC_RelayControl_+12v = female pin header, 8 pins [form="♀ (female)"]
  Switch_Input = 74HC165 [package="DIP (Dual Inline) [THT]"]
  R9 = Resistor [tolerance=±10% resistance=1k package="0805 [SMD]"]
  D9 = Zener Diode [part_number=1N4732A breakdown_voltage=3.6V package="300 mil [THT]"]
  D10 = Zener Diode [part_number=1N4732A breakdown_voltage=3.6V package="300 mil [THT]"]
  R10 = Resistor [tolerance=±5% resistance=1k package=THT]
  D11 = Zener Diode [part_number=1N4732A breakdown_voltage=3.6V package="300 mil [THT]"]
  R11 = Resistor [tolerance=±5% resistance=1k package=THT]
  R12 = Resistor [tolerance=±5% resistance=1k package=THT]
  D12 = Zener Diode [part_number=1N4732A breakdown_voltage=3.6V package="300 mil [THT]"]
  D13 = Zener Diode [part_number=1N4732A breakdown_voltage=3.6V package="300 mil [THT]"]
  R13 = Resistor [tolerance=±5% resistance=1k package=THT]
  D14 = Zener Diode [part_number=1N4732A breakdown_voltage=3.6V package="300 mil [THT]"]
  R14 = Resistor [tolerance=±5% resistance=1k package=THT]
  D15 = Zener Diode [part_number=1N4732A breakdown_voltage=3.6V package="300 mil [THT]"]
  R15 = Resistor [tolerance=±5% resistance=1k package=THT]
  D16 = Zener Diode [part_number=1N4732A breakdown_voltage=3.6V package="300 mil [THT]"]
  R16 = Resistor [tolerance=±5% resistance=1k package=THT]
  Switch_Input_+12v = female pin header, 8 pins [form="♀ (female)"]

nets:
  Ground: ARDUINO1.GND, Ground1.pin1, R2.Pin_0, BT4_0_HM-12.GND, Output_Control.GND, Output_Control.Q7', OC_Q9.E, OC_Q10.E, OC_Q11.E, OC_Q12.E, OC_Q13.E, OC_Q14.E, OC_Q15.E, OC_Q16.E, Switch_Input.GND, Switch_Input.DS, Switch_Input.!CE, R9.Pin_0, R10.Pin_1, R11.Pin_0, R12.Pin_0, R13.Pin_0, R14.Pin_0, R15.Pin_0, R16.Pin_0
  N1: ARDUINO1.A6, Switch_Input.!PL
  N2: ARDUINO1.A5, R2.Pin_1, Output_Control.OE
  N3: ARDUINO1.A4, Output_Control.ST_CP
  N4: ARDUINO1.A3, Output_Control.SH_CP, Switch_Input.CP
  N5: ARDUINO1.A2, Output_Control.DS, Switch_Input.Q7
  N6: ARDUINO1.A1, BT4_0_HM-12.RXD
  N7: ARDUINO1.A0, BT4_0_HM-12.TXD
  N8: ARDUINO1.3V3, BT4_0_HM-12.VCC_+3v
  VCC: +5v1.pin1, Output_Control.MR, Output_Control.VCC, Switch_Input.Vcc
  OC_2: Output_Control.Q1, OC_R10.Pin_0
  OC_3: Output_Control.Q2, OC_R11.Pin_0
  OC_4: Output_Control.Q3, OC_R12.Pin_0
  OC_5: Output_Control.Q4, OC_R13.Pin_0
  OC_6: Output_Control.Q5, OC_R14.Pin_0
  OC_7: Output_Control.Q6, OC_R15.Pin_0
  OC_8: Output_Control.Q7, OC_R16.Pin_0
  OC_1: Output_Control.Q0, OC_R9.Pin_1
  N9: OC_Q9.B, OC_R9.Pin_0
  OC_I1: OC_Q9.C, OC_RelayControl_+12v.pin1
  N10: OC_Q10.B, OC_R10.Pin_1
  OC_I2: OC_Q10.C, OC_RelayControl_+12v.pin2
  N11: OC_Q11.B, OC_R11.Pin_1
  OC_I3: OC_Q11.C, OC_RelayControl_+12v.pin3
  N12: OC_Q12.B, OC_R12.Pin_1
  OC_I4: OC_Q12.C, OC_RelayControl_+12v.pin4
  N13: OC_Q13.B, OC_R13.Pin_1
  OC_I5: OC_Q13.C, OC_RelayControl_+12v.pin5
  N14: OC_Q14.B, OC_R14.Pin_1
  OC_I6: OC_Q14.C, OC_RelayControl_+12v.pin6
  N15: OC_Q15.B, OC_R15.Pin_1
  OC_I7: OC_Q15.C, OC_RelayControl_+12v.pin7
  N16: OC_Q16.B, OC_R16.Pin_1
  OC_I8: OC_Q16.C, OC_RelayControl_+12v.pin8
  IC_4: Switch_Input.D4, D13.anode, R13.Pin_1
  IC_5: Switch_Input.D5, D14.anode, R14.Pin_1
  IC_6: Switch_Input.D6, D15.anode, R15.Pin_1
  IC_7: Switch_Input.D7, D16.anode, R16.Pin_1
  IC_0: Switch_Input.D0, R9.Pin_1, D9.anode
  IC_1: Switch_Input.D1, D10.anode, R10.Pin_0
  IC_2: Switch_Input.D2, D11.anode, R11.Pin_1
  IC_3: Switch_Input.D3, R12.Pin_1, D12.anode
  Sw_I0: D9.cathode, Switch_Input_+12v.pin1
  Sw_I1: D10.cathode, Switch_Input_+12v.pin2
  Sw_I2: D11.cathode, Switch_Input_+12v.pin3
  Sw_I3: D12.cathode, Switch_Input_+12v.pin4
  Sw_I4: D13.cathode, Switch_Input_+12v.pin5
  Sw_I5: D14.cathode, Switch_Input_+12v.pin6
  Sw_I6: D15.cathode, Switch_Input_+12v.pin7
  Sw_I7: D16.cathode, Switch_Input_+12v.pin8

custom parts:
  74HC165: Asynchrounous parallel-in serial-out.
