# Fritzing sketch Power Module (saved by Fritzing 0.9.2b)
perfboards: 1

parts:
  Output_Control = 74HC595 [package="DIP16 [THT]"]
  OC_Q1 = TRANSISTOR_NPN [package=to-92]
  OC_R1 = Resistor [tolerance=±5% resistance=10k package="0805 [SMD]"]
  Ground = female pin header, 1 pin [form="♀ (female)"]
  +5v = female pin header, 1 pin [form="♀ (female)"]
  OC_Input_pins_+12v = female pin header, 8 pins [form="♀ (female)"]
  OC_Q2 = TRANSISTOR_NPN [package=to-92]
  OC_R2 = Resistor [tolerance=±5% resistance=10k package="0805 [SMD]"]
  OC_Q3 = TRANSISTOR_NPN [package=to-92]
  OC_R3 = Resistor [tolerance=±5% resistance=10k package="0805 [SMD]"]
  OC_Q4 = TRANSISTOR_NPN [package=to-92]
  OC_R4 = Resistor [tolerance=±5% resistance=10k package="0805 [SMD]"]
  OC_Q5 = TRANSISTOR_NPN [package=to-92]
  OC_R5 = Resistor [tolerance=±5% resistance=10k package="0805 [SMD]"]
  OC_Q6 = TRANSISTOR_NPN [package=to-92]
  OC_R6 = Resistor [tolerance=±5% resistance=10k package="0805 [SMD]"]
  OC_Q7 = TRANSISTOR_NPN [package=to-92]
  OC_R7 = Resistor [tolerance=±5% resistance=10k package="0805 [SMD]"]
  OC_Q8 = TRANSISTOR_NPN [package=to-92]
  OC_R8 = Resistor [tolerance=±5% resistance=10k package="0805 [SMD]"]
  OC_Control_Pins = female pin header, 5 pins [form="♀ (female)"]

nets:
  OC_2: Output_Control.Q1, OC_R2.Pin_0
  OC_3: Output_Control.Q2, OC_R3.Pin_0
  OC_4: Output_Control.Q3, OC_R4.Pin_0
  OC_5: Output_Control.Q4, OC_R5.Pin_0
  OC_6: Output_Control.Q5, OC_R6.Pin_0
  OC_7: Output_Control.Q6, OC_R7.Pin_0
  OC_8: Output_Control.Q7, OC_R8.Pin_0
  Common: Output_Control.GND, OC_Q1.E, Ground.pin1, OC_Q2.E, OC_Q3.E, OC_Q4.E, OC_Q5.E, OC_Q6.E, OC_Q7.E, OC_Q8.E
  OC_Out: Output_Control.Q7', OC_Control_Pins.pin1
  Source: Output_Control.MR, Output_Control.VCC, +5v.pin1
  OC_Clock: Output_Control.SH_CP, OC_Control_Pins.pin2
  OC_Latch: Output_Control.ST_CP, OC_Control_Pins.pin3
  OC_Enabled: Output_Control.OE, OC_Control_Pins.pin4
  OC_Data: Output_Control.DS, OC_Control_Pins.pin5
  OC_1: Output_Control.Q0, OC_R1.Pin_1
  N1: OC_Q1.B, OC_R1.Pin_0
  OC_I1: OC_Q1.C, OC_Input_pins_+12v.pin1
  OC_I2: OC_Input_pins_+12v.pin2, OC_Q2.C
  OC_I3: OC_Input_pins_+12v.pin3, OC_Q3.C
  OC_I4: OC_Input_pins_+12v.pin4, OC_Q4.C
  OC_I5: OC_Input_pins_+12v.pin5, OC_Q5.C
  OC_I6: OC_Input_pins_+12v.pin6, OC_Q6.C
  OC_I7: OC_Input_pins_+12v.pin7, OC_Q7.C
  OC_I8: OC_Input_pins_+12v.pin8, OC_Q8.C
  N2: OC_Q2.B, OC_R2.Pin_1
  N3: OC_Q3.B, OC_R3.Pin_1
  N4: OC_Q4.B, OC_R4.Pin_1
  N5: OC_Q5.B, OC_R5.Pin_1
  N6: OC_Q6.B, OC_R6.Pin_1
  N7: OC_Q7.B, OC_R7.Pin_1
  N8: OC_Q8.B, OC_R8.Pin_1
