# Fritzing sketch Switch Module (saved by Fritzing 0.9.2b)
perfboards: 1

parts:
  Sw_Input = 74HC165 [package="DIP (Dual Inline) [THT]"]
  RC = Resistor [tolerance=±10% resistance=100 package="0805 [SMD]"]
  RL = Resistor [tolerance=±10% resistance=1k package="0805 [SMD]"]
  1 = Header 1 [package=1x01_offset]
  R1 = Resistor [tolerance=±10% resistance=1k package="0805 [SMD]"]
  +5v = Header 1 [package=1x01_offset]
  Ground = female pin header, 1 pin [form="♀ (female)"]
  D1 = Zener Diode [part_number=1N4732A breakdown_voltage=3.6V package="300 mil [THT]"]
  D2 = Zener Diode [part_number=1N4732A breakdown_voltage=3.6V package="300 mil [THT]"]
  2 = female pin header, 1 pin [form="♀ (female)"]
  R2 = Resistor [tolerance=±5% resistance=1k package=THT]
  D3 = Zener Diode [part_number=1N4732A breakdown_voltage=3.6V package="300 mil [THT]"]
  3 = female pin header, 1 pin [form="♀ (female)"]
  R3 = Resistor [tolerance=±5% resistance=1k package=THT]
  R4 = Resistor [tolerance=±5% resistance=1k package=THT]
  4 = female pin header, 1 pin [form="♀ (female)"]
  D4 = Zener Diode [part_number=1N4732A breakdown_voltage=3.6V package="300 mil [THT]"]
  D5 = Zener Diode [part_number=1N4732A breakdown_voltage=3.6V package="300 mil [THT]"]
  R5 = Resistor [tolerance=±5% resistance=1k package=THT]
  5 = female pin header, 1 pin [form="♀ (female)"]
  D6 = Zener Diode [part_number=1N4732A breakdown_voltage=3.6V package="300 mil [THT]"]
  R6 = Resistor [tolerance=±5% resistance=1k package=THT]
  6 = female pin header, 1 pin [form="♀ (female)"]
  D7 = Zener Diode [part_number=1N4732A breakdown_voltage=3.6V package="300 mil [THT]"]
  7 = female pin header, 1 pin [form="♀ (female)"]
  R7 = Resistor [tolerance=±5% resistance=1k package=THT]
  D8 = Zener Diode [part_number=1N4732A breakdown_voltage=3.6V package="300 mil [THT]"]
  8 = female pin header, 1 pin [form="♀ (female)"]
  R8 = Resistor [tolerance=±5% resistance=1k package=THT]
  Load = female pin header, 1 pin [form="♀ (female)"]
  Clock = female pin header, 1 pin [form="♀ (female)"]
  Data = female pin header, 1 pin [form="♀ (female)"]

nets:
  Load: Sw_Input.!PL, RL.Pin_0, Load.pin1
  Clock: Sw_Input.CP, RC.Pin_0, Clock.pin1
  5: Sw_Input.D4, D5.anode, R5.Pin_1
  6: Sw_Input.D5, D6.anode, R6.Pin_1
  7: Sw_Input.D6, D7.anode, R7.Pin_1
  8: Sw_Input.D7, D8.anode, R8.Pin_1
  Common: Sw_Input.GND, Sw_Input.DS, Sw_Input.!CE, RC.Pin_1, R1.Pin_0, Ground.pin1, R2.Pin_1, R3.Pin_0, R4.Pin_0, R5.Pin_0, R6.Pin_0, R7.Pin_0, R8.Pin_0
  Data: Sw_Input.Q7, Data.pin1
  1: Sw_Input.D0, R1.Pin_1, D1.anode
  2: Sw_Input.D1, D2.anode, R2.Pin_0
  3: Sw_Input.D2, D3.anode, R3.Pin_1
  4: Sw_Input.D3, R4.Pin_1, D4.anode
  Source: Sw_Input.Vcc, RL.Pin_1, +5v.1
  N1: 1.1, D1.cathode
  N2: D2.cathode, 2.pin1
  N3: D3.cathode, 3.pin1
  N4: 4.pin1, D4.cathode
  N5: D5.cathode, 5.pin1
  N6: D6.cathode, 6.pin1
  N7: D7.cathode, 7.pin1
  N8: D8.cathode, 8.pin1

custom parts:
  74HC165: Asynchrounous parallel-in serial-out.
